# Fritzing sketch Perfilador KdUINO (saved by Fritzing 0.9.3b)

parts:
  Componente1 = Arduino Uno (Rev3)  # not connected
  Componente2 = Memoire 1.0 - SD card log shield
  LED1 = smd LED [color="Red (633nm)" package="1206 [SMD]"]
  S1 = Square Pushbutton
  J1 = Camdenboss CTB0158-3 [part_number=CTB0158-3 package=THT]
  J2 = Camdenboss CTB0158-3 [part_number=CTB0158-3 package=THT]
  J3 = Peltier Element

nets:
  N1: Componente2.N$21, J2.pin3
  N2: Componente2.N$30, LED1.cathode, S1.leg1
  N3: Componente2.N$37, J2.pin1
  N4: Componente2.N$38, J2.pin2
  N5: Componente2.N$67, J1.pin1
  N6: Componente2.N$90, J1.pin2
  N7: Componente2.N$91, J1.pin3
  N8: LED1.anode, J2.terminal_1
  N9: S1.leg0, J1.terminal_3
  N10: J1.terminal_1, J3.pin2
  N11: J1.terminal_2, J3.pin1
